# Fritzing sketch krets (saved by Fritzing 0.9.4)
breadboards: 1

parts:
  Part2 = Arduino Nano (Rev3.0) (ICSP)
  LED1 = smd LED [color="Blue (525nm)" package="0603 [SMD]"]
  LED2 = smd LED [color="Green (570nm)" package="0603 [SMD]"]
  LED3 = smd LED [color="Red (633nm)" package="0603 [SMD]"]
  LED4 = smd LED [color="Yellow (595nm)" package="0603 [SMD]"]
  R1 = Resistor [tolerance=±5% resistance=220 package="0603 [SMD]"]
  R2 = Resistor [tolerance=±5% resistance=220 package="0603 [SMD]"]
  R3 = Resistor [tolerance=±5% resistance=220 package="0603 [SMD]"]
  R4 = Resistor [tolerance=±5% resistance=220 package="0603 [SMD]"]
  R5 = Resistor [tolerance=±5% resistance=100k package="0603 [SMD]"]
  S1 = Momentary Switch [package=ksa_sealed_tac_switch]
  S2 = Momentary Switch [package=ksa_sealed_tac_switch]
  S3 = Momentary Switch [package=ksa_sealed_tac_switch]
  S4 = Momentary Switch [package=ksa_sealed_tac_switch]
  S5 = Momentary Switch [package=ksa_sealed_tac_switch]
  S6 = Momentary Switch [package=ksa_sealed_tac_switch]
  S7 = Momentary Switch [package=ksa_sealed_tac_switch]
  S8 = Momentary Switch [package=ksa_sealed_tac_switch]
  R6 = Resistor [tolerance=±5% resistance=100k package="0603 [SMD]"]
  R7 = Resistor [tolerance=±5% resistance=100k package="0603 [SMD]"]
  R8 = Resistor [tolerance=±5% resistance=100k package="0603 [SMD]"]
  R9 = Resistor [tolerance=±5% resistance=100k package="0603 [SMD]"]
  R10 = Resistor [tolerance=±5% resistance=100k package="0603 [SMD]"]
  R11 = Resistor [tolerance=±5% resistance=100k package="0603 [SMD]"]
  R12 = Resistor [tolerance=±5% resistance=100k package="0603 [SMD]"]

nets:
  N1: Part2.D5, S4.3
  N2: Part2.D6, S3.3
  N3: Part2.D7, S2.3
  N4: Part2.D8, S1.3
  N5: Part2.D9, R4.Pin_1
  N6: Part2.D10, R3.Pin_1
  N7: Part2.D11/MOSI, R2.Pin_1
  N8: Part2.D12/MISO, R1.Pin_1
  N9: Part2.GND, Part2.RESET, LED1.anode, LED2.anode, LED3.anode, LED4.anode, R5.Pin_1, R6.Pin_1, R7.Pin_1, R8.Pin_1, R9.Pin_1, R10.Pin_1, R11.Pin_1, R12.Pin_1
  N10: Part2.5V, Part2.A7, S1.2, S2.2, S3.2, S4.2, S5.2, S6.2, S7.2, S8.2
  N11: Part2.A3, S8.3
  N12: Part2.A2, S7.3
  N13: Part2.A1, S6.3
  N14: Part2.A0, S5.3
  N15: LED1.cathode, R1.Pin_0
  N16: LED2.cathode, R2.Pin_0
  N17: LED3.cathode, R3.Pin_0
  N18: LED4.cathode, R4.Pin_0
  N19: R5.Pin_0, S1.4
  N20: S2.4, R6.Pin_0
  N21: S3.4, R7.Pin_0
  N22: S4.4, R8.Pin_0
  N23: S5.4, R9.Pin_0
  N24: S6.4, R10.Pin_0
  N25: S7.4, R11.Pin_0
  N26: S8.4, R12.Pin_0
